// Logisim project main.circ as structural Verilog: 12 circuits, main circuit main
module main (
);

  wire and_1_out, btn_peaton_reset_1_out_7, button_1_out, button_2_out, clock_1_out, clock_2_out,
       contador_1_a, contador_1_b, contador_1_c, contador_1_d, contador_7_seg_1_a, contador_7_seg_1_b,
       contador_7_seg_1_c, contador_7_seg_1_d, ctrl_auto_1_amarillo, ctrl_auto_1_rojo, ctrl_auto_1_verde,
       ctrl_peaton_1_rojo, ctrl_peaton_1_verde, d1_1_out_5, d1_1_out_6, d1_1_out_7, d2_1_out_5, d2_1_out_6,
       d2_1_out_7, d2_1_s0, d2_1_s1, d2_1_s2, d2_1_s3, not_1_out, not_2_out, not_3_out, not_4_out, or_1_out,
       or_2_out, or_3_out, s_auto_1_amarillo_2, s_auto_1_rojo_2, s_auto_1_verde_2, s_peaton_1_peaton,
       s_peaton_1_verde_2;

  Clock #(.highDuration(5), .lowDuration(5)) clock_1 (.out(clock_1_out));
  Clock clock_2 (.out(clock_2_out));
  Button button_1 (.out(button_1_out));
  not not_1 (not_1_out, clock_1_out);
  not not_2 (not_2_out, button_1_out);
  or or_1 (or_1_out, button_1_out, btn_peaton_reset_1_out_7);
  Contador contador_1 (
    .Jk(not_2_out), .Clock(not_1_out), .Reset(or_1_out), .A(contador_1_a), .B(contador_1_b),
    .C(contador_1_c), .D(contador_1_d));
  not not_3 (not_3_out, contador_7_seg_1_b);
  not not_4 (not_4_out, contador_7_seg_1_d);
  and and_1 (and_1_out, contador_7_seg_1_a, not_3_out, contador_7_seg_1_c, not_4_out);
  or or_2 (or_2_out, button_1_out, and_1_out);
  Contador_7_seg contador_7_seg_1 (
    .Jk(d1_1_out_7), .Clock(clock_2_out), .Reset(or_2_out), .A(contador_7_seg_1_a), .B(contador_7_seg_1_b),
    .C(contador_7_seg_1_c), .D(contador_7_seg_1_d));
  Btn_Peaton___Reset btn_peaton_reset_1 (
    .A(contador_1_a), .B(contador_1_b), .C(contador_1_c), .D(contador_1_d), .Btn_Peaton(button_2_out),
    .in_6(button_1_out), .out_7(btn_peaton_reset_1_out_7));
  Ctrl_AUTO ctrl_auto_1 (
    .A(contador_1_a), .B(contador_1_b), .C(contador_1_c), .D(contador_1_d), .ROJO(ctrl_auto_1_rojo),
    .AMARILLO(ctrl_auto_1_amarillo), .VERDE(ctrl_auto_1_verde));
  Ctrl_PEATON ctrl_peaton_1 (
    .A(contador_1_a), .B(contador_1_b), .C(contador_1_c), .D(contador_1_d), .Clock(clock_2_out),
    .Rojo(ctrl_peaton_1_rojo), .Verde(ctrl_peaton_1_verde));
  D1 d1_1 (
    .A(contador_1_a), .B(contador_1_b), .C(contador_1_c), .D(contador_1_d), .out_5(d1_1_out_5),
    .out_6(d1_1_out_6), .out_7(d1_1_out_7));
  D2 d2_1 (
    .A(contador_7_seg_1_a), .B(contador_7_seg_1_b), .C(contador_7_seg_1_c), .D(contador_7_seg_1_d),
    .out_5(d2_1_out_5), .out_6(d2_1_out_6), .out_7(d2_1_out_7), .S3(d2_1_s3), .S2(d2_1_s2), .S1(d2_1_s1),
    .S0(d2_1_s0));
  _7_Segment_Display u_7_segment_display_1 (
    .f(d1_1_out_6), .a(d1_1_out_6), .b(or_3_out), .e(d1_1_out_6), .d(d1_1_out_6), .c(or_3_out));  // open: g, dp
  S__Auto s_auto_1 (
    .Reset(button_1_out), .ROJO(ctrl_auto_1_rojo), .AMARILLO(ctrl_auto_1_amarillo),
    .VERDE(ctrl_auto_1_verde), .ROJO_2(s_auto_1_rojo_2), .AMARILLO_2(s_auto_1_amarillo_2),
    .VERDE_2(s_auto_1_verde_2));
  S__Peaton s_peaton_1 (
    .Reset(button_1_out), .ROJO(ctrl_peaton_1_rojo), .VERDE(ctrl_peaton_1_verde), .PEATON(s_peaton_1_peaton),
    .VERDE_2(s_peaton_1_verde_2));
  or or_3 (or_3_out, d1_1_out_5, d1_1_out_6);
  _7_Segment_Display u_7_segment_display_2 (
    .g(d2_1_s3), .f(d2_1_out_7), .a(d2_1_out_6), .b(d2_1_out_5), .e(d2_1_s2), .d(d2_1_s1), .c(d2_1_s0));  // open: dp
  Button button_2 (.out(button_2_out));
  LED led_1 (.in(s_auto_1_rojo_2));
  LED led_2 (.in(s_auto_1_amarillo_2));
  LED led_3 (.in(s_auto_1_verde_2));
  LED led_4 (.in(s_peaton_1_peaton));
  LED led_5 (.in(s_peaton_1_verde_2));

  // Notes on the sheet:
  //   INICIALIZACION
  //   BOTON PEATON
  //   AUTO
  //   PEATON
  //   ROJO
  //   AMARILLO
  //   VERDE
  //   ROJO
  //   VERDE
endmodule

module Ctrl_PEATON (
  input  A,
  input  B,
  input  C,
  input  D,
  input  Clock,
  output Rojo,
  output Verde
);

  wire and_1_out, and_2_out, and_3_out, and_4_out, j_k_ff_1_qn, not_1_out, not_2_out, not_3_out, not_4_out,
       not_5_out, not_6_out, or_1_out;

  not not_1 (not_1_out, A);
  not not_2 (not_2_out, B);
  not not_3 (not_3_out, C);
  not not_4 (not_4_out, D);
  not not_5 (not_5_out, A);
  and and_1 (and_1_out, A, not_2_out, not_3_out, not_4_out);
  and and_2 (and_2_out, not_5_out, B, C, D);
  and and_3 (and_3_out, not_1_out, not_2_out);
  and and_4 (and_4_out, not_1_out, not_3_out, not_4_out);
  or or_1 (or_1_out, and_1_out, and_2_out);
  or or_2 (Rojo, and_3_out, and_4_out);
  not not_6 (not_6_out, Rojo);
  J_K_Flip_Flop j_k_ff_1 (.J(or_1_out), .clk(Clock), .K(or_1_out), .Qn(j_k_ff_1_qn));  // open: Q, preset, en, reset
  and and_5 (Verde, not_6_out, j_k_ff_1_qn);
endmodule

module Ctrl_AUTO (
  input  A,
  input  B,
  input  C,
  input  D,
  output ROJO,
  output AMARILLO,
  output VERDE
);

  wire and_1_out, and_2_out, and_3_out, not_1_out, not_2_out, not_3_out, not_4_out, not_5_out, not_6_out,
       not_7_out, not_8_out, or_1_out;

  not not_1 (not_1_out, A);
  not not_2 (not_2_out, B);
  and and_1 (and_1_out, not_1_out, not_2_out, C, D);
  not not_3 (not_3_out, A);
  not not_4 (not_4_out, B);
  not not_5 (not_5_out, C);
  not not_6 (not_6_out, A);
  not not_7 (not_7_out, B);
  not not_8 (not_8_out, D);
  or or_1 (or_1_out, A, B);
  and and_2 (and_2_out, not_3_out, not_4_out, not_5_out);
  and and_3 (and_3_out, not_6_out, not_7_out, not_8_out);
  buf or_2 (ROJO, or_1_out);  // OR_Gate
  buf or_3 (AMARILLO, and_1_out);  // OR_Gate
  or or_4 (VERDE, and_2_out, and_3_out);
endmodule

module Btn_Peaton___Reset (
  input  A,
  input  B,
  input  C,
  input  D,
  input  Btn_Peaton,
  input  in_6,
  output out_7
);

  wire and_1_out, and_2_out, d_ff_1_qn, not_1_out, not_2_out, or_1_out;

  not not_1 (not_1_out, B);
  not not_2 (not_2_out, C);
  and and_1 (and_1_out, A, not_1_out, not_2_out, D);
  and and_2 (and_2_out, Btn_Peaton, out_7);
  or or_1 (or_1_out, and_1_out, in_6);
  D_Flip_Flop d_ff_1 (.clk(or_1_out), .D(d_ff_1_qn), .Q(out_7), .Qn(d_ff_1_qn), .reset(and_2_out));  // open: preset, en
endmodule

module S__Auto (
  input  Reset,
  input  ROJO,
  input  AMARILLO,
  input  VERDE,
  output ROJO_2,
  output AMARILLO_2,
  output VERDE_2
);

  or or_1 (ROJO_2, Reset, ROJO);
  or or_2 (AMARILLO_2, Reset, AMARILLO);
  or or_3 (VERDE_2, Reset, VERDE);

  // Notes on the sheet:
  //   AUTO
endmodule

module S__Peaton (
  input  Reset,
  input  ROJO,
  input  VERDE,
  output PEATON,
  output VERDE_2
);

  or or_1 (PEATON, Reset, ROJO);
  or or_2 (VERDE_2, Reset, VERDE);

  // Notes on the sheet:
  //   ROJO
endmodule

module Contador (
  input  Jk,
  input  Clock,
  input  Reset,
  output A,
  output B,
  output C,
  output D
);

  wire j_k_ff_1_qn, j_k_ff_2_qn, j_k_ff_3_qn, j_k_ff_4_qn;

  J_K_Flip_Flop j_k_ff_1 (.J(Jk), .clk(Clock), .K(Jk), .Q(D), .Qn(j_k_ff_1_qn), .reset(Reset));  // open: preset, en
  J_K_Flip_Flop j_k_ff_2 (
    .J(Jk), .clk(j_k_ff_1_qn), .K(Jk), .Q(C), .Qn(j_k_ff_2_qn), .reset(Reset));  // open: preset, en
  J_K_Flip_Flop j_k_ff_3 (
    .J(Jk), .clk(j_k_ff_2_qn), .K(Jk), .Q(B), .Qn(j_k_ff_3_qn), .reset(Reset));  // open: preset, en
  J_K_Flip_Flop j_k_ff_4 (
    .J(Jk), .clk(j_k_ff_3_qn), .K(Jk), .Q(A), .Qn(j_k_ff_4_qn), .reset(Reset));  // open: preset, en
endmodule

module D1 (
  input  A,
  input  B,
  input  C,
  input  D,
  output out_5,
  output out_6,
  output out_7
);

  wire and_1_out, and_2_out, and_3_out, not_1_out, not_2_out, not_3_out, not_4_out, not_5_out, not_6_out,
       not_7_out, or_1_out, or_3_out;

  not not_1 (not_1_out, A);
  not not_2 (not_2_out, B);
  not not_3 (not_3_out, C);
  not not_4 (not_4_out, D);
  and and_1 (and_1_out, not_1_out, B, C, D);
  and and_2 (and_2_out, A, not_2_out, not_3_out, not_4_out);
  not not_5 (not_5_out, A);
  or or_1 (or_1_out, C, D);
  and and_3 (and_3_out, not_5_out, B, or_1_out);
  or or_2 (out_7, and_3_out, and_2_out);
  or or_3 (or_3_out, A, and_3_out);
  not not_6 (not_6_out, or_3_out);
  and and_4 (out_5, or_3_out, not_7_out);
  not not_7 (not_7_out, out_6);
  or or_4 (out_6, not_6_out, and_2_out, and_1_out);

  // Notes on the sheet:
  //   JK PARA EL VISOR 2
  //   S6 - S0 = 1
  //   S6 S5 S4 S2 S1 S0 = 0
endmodule

module Referencia_7_seg (
  input  S4,
  input  S5,
  input  S3,
  input  S6,
  input  S2,
  input  S1,
  input  S0,
  input  S7
);

  _7_Segment_Display u_7_segment_display_1 (.g(S3), .f(S4), .a(S5), .b(S6), .e(S2), .d(S1), .c(S0), .dp(S7));
endmodule

module D2 (
  input  A,
  input  B,
  input  C,
  input  D,
  output out_5,
  output out_6,
  output out_7,
  output S3,
  output S2,
  output S1,
  output S0
);

  wire and_1_out, and_2_out, and_3_out, and_4_out, and_5_out, and_6_out, and_7_out, and_8_out, and_9_out,
       and_10_out, and_11_out, and_12_out, and_13_out, and_14_out, and_15_out, and_16_out, and_17_out,
       and_18_out, and_19_out, and_20_out, and_21_out, and_22_out, and_23_out, and_24_out, and_25_out,
       not_1_out, not_2_out, not_3_out, not_4_out, not_5_out, not_6_out, not_7_out, not_8_out, not_9_out,
       not_10_out, not_11_out, not_12_out, not_13_out, not_14_out, not_15_out, not_16_out, not_17_out,
       not_18_out, not_19_out, not_20_out, not_21_out, not_22_out, not_23_out, not_24_out, not_25_out,
       not_26_out, not_27_out, not_28_out, not_29_out, not_30_out, not_31_out, not_32_out, not_33_out,
       not_34_out, not_35_out, not_36_out, not_37_out, not_38_out, not_39_out, not_40_out, not_41_out,
       not_42_out, not_43_out, not_44_out, not_45_out, not_46_out, not_47_out, not_48_out, not_49_out,
       not_50_out;

  not not_1 (not_1_out, B);
  not not_2 (not_2_out, C);
  not not_3 (not_3_out, B);
  not not_4 (not_4_out, C);
  not not_5 (not_5_out, D);
  not not_6 (not_6_out, A);
  not not_7 (not_7_out, B);
  not not_8 (not_8_out, C);
  not not_9 (not_9_out, D);
  not not_10 (not_10_out, A);
  not not_11 (not_11_out, C);
  not not_12 (not_12_out, A);
  not not_13 (not_13_out, D);
  not not_14 (not_14_out, D);
  not not_15 (not_15_out, C);
  not not_16 (not_16_out, D);
  not not_17 (not_17_out, B);
  not not_18 (not_18_out, D);
  not not_19 (not_19_out, C);
  not not_20 (not_20_out, D);
  not not_21 (not_21_out, B);
  not not_22 (not_22_out, D);
  not not_23 (not_23_out, A);
  not not_24 (not_24_out, C);
  and and_1 (and_1_out, not_1_out, D);
  not not_25 (not_25_out, A);
  not not_26 (not_26_out, B);
  not not_27 (not_27_out, C);
  not not_28 (not_28_out, D);
  and and_2 (and_2_out, A, not_29_out);
  not not_29 (not_29_out, D);
  not not_30 (not_30_out, A);
  and and_3 (and_3_out, not_30_out, D);
  and and_4 (and_4_out, B, not_2_out);
  and and_5 (and_5_out, not_3_out, C);
  not not_31 (not_31_out, A);
  not not_32 (not_32_out, B);
  not not_33 (not_33_out, C);
  not not_34 (not_34_out, D);
  and and_6 (and_6_out, B, not_4_out);
  and and_7 (and_7_out, C, not_5_out);
  and and_8 (and_8_out, not_6_out, not_7_out, D);
  not not_35 (not_35_out, A);
  not not_36 (not_36_out, B);
  not not_37 (not_37_out, C);
  not not_38 (not_38_out, D);
  and and_9 (and_9_out, A, not_8_out, not_9_out);
  and and_10 (and_10_out, not_10_out, not_11_out, D);
  and and_11 (and_11_out, not_12_out, C, not_13_out);
  and and_12 (and_12_out, A, not_14_out);
  and and_13 (and_13_out, B, not_15_out, not_16_out);
  and and_14 (and_14_out, not_17_out, C, not_18_out);
  not not_39 (not_39_out, A);
  not not_40 (not_40_out, B);
  not not_41 (not_41_out, C);
  not not_42 (not_42_out, D);
  and and_15 (and_15_out, B, not_19_out);
  and and_16 (and_16_out, B, D);
  and and_17 (and_17_out, A, not_20_out);
  and and_18 (and_18_out, not_21_out, C, not_22_out);
  and and_19 (and_19_out, not_23_out, not_24_out, D);
  not not_43 (not_43_out, A);
  not not_44 (not_44_out, B);
  not not_45 (not_45_out, C);
  not not_46 (not_46_out, D);
  not not_47 (not_47_out, A);
  not not_48 (not_48_out, B);
  not not_49 (not_49_out, C);
  not not_50 (not_50_out, D);
  and and_20 (and_20_out, not_25_out, not_26_out, not_27_out, not_28_out);
  and and_21 (and_21_out, not_31_out, not_32_out, not_33_out, not_34_out);
  and and_22 (and_22_out, not_35_out, not_36_out, not_37_out, not_38_out);
  and and_23 (and_23_out, not_39_out, not_40_out, not_41_out, not_42_out);
  and and_24 (and_24_out, not_43_out, not_44_out, not_45_out, not_46_out);
  and and_25 (and_25_out, not_47_out, not_48_out, not_49_out, not_50_out);
  or or_1 (out_5, A, C, and_1_out, and_20_out);
  or or_2 (out_6, and_2_out, and_3_out, and_4_out, and_5_out, and_21_out);
  or or_3 (out_7, and_6_out, and_7_out, and_8_out, and_22_out);
  or or_4 (S3, B, and_9_out, and_10_out, and_11_out);
  or or_5 (S2, and_12_out, and_13_out, and_14_out, and_23_out);
  or or_6 (S1, and_15_out, and_16_out, and_17_out, and_18_out, and_19_out, and_24_out);
  or or_7 (S0, B, C, D, and_25_out);

  // Notes on the sheet:
  //   S6
  //   S5
  //   S4
endmodule

module Contador_7_seg (
  input  Jk,
  input  Clock,
  input  Reset,
  output A,
  output B,
  output C,
  output D
);

  wire j_k_ff_1_q, j_k_ff_1_qn, j_k_ff_2_qn, j_k_ff_3_qn;

  J_K_Flip_Flop j_k_ff_1 (
    .J(Jk), .clk(Clock), .K(Jk), .Q(j_k_ff_1_q), .Qn(j_k_ff_1_qn), .reset(Reset));  // open: preset, en
  J_K_Flip_Flop j_k_ff_2 (
    .J(Jk), .clk(j_k_ff_1_qn), .K(Jk), .Q(C), .Qn(j_k_ff_2_qn), .reset(Reset));  // open: preset, en
  or or_1 (D, j_k_ff_1_q, Reset);
  J_K_Flip_Flop j_k_ff_3 (
    .J(Jk), .clk(j_k_ff_2_qn), .K(Jk), .Q(B), .Qn(j_k_ff_3_qn), .reset(Reset));  // open: preset, en
  J_K_Flip_Flop j_k_ff_4 (.J(Jk), .clk(j_k_ff_3_qn), .K(Jk), .Q(A), .reset(Reset));  // open: Qn, preset, en
endmodule

module Reset_contador_7_seg (
  input  A,
  input  B,
  input  C,
  input  D,
  output Verde,
  output Verde_2
);

  wire and_1_out, and_2_out, and_3_out, and_4_out, not_1_out, not_2_out, not_3_out, not_4_out, not_5_out,
       not_6_out, not_7_out, not_8_out, or_2_out;

  not not_1 (not_1_out, A);
  not not_2 (not_2_out, B);
  not not_3 (not_3_out, C);
  not not_4 (not_4_out, D);
  not not_5 (not_5_out, B);
  not not_6 (not_6_out, C);
  not not_7 (not_7_out, D);
  not not_8 (not_8_out, A);
  and and_1 (and_1_out, A, not_5_out, not_6_out, not_7_out);
  and and_2 (and_2_out, not_8_out, B, C, D);
  and and_3 (and_3_out, not_1_out, not_2_out);
  and and_4 (and_4_out, not_1_out, not_3_out, not_4_out);
  or or_1 (Verde_2, and_1_out, and_2_out);
  or or_2 (or_2_out, and_3_out, and_4_out);
  not not_9 (Verde, or_2_out);
endmodule
